# Fritzing sketch remote control (saved by Fritzing 0.9.3b)

parts:
  Componente1 = Arduino Nano (Rev3.0)
  Componente4 = I2C level shifter bidirectional
  JP1 = Header 3 [package=screwterminal-3.5mm-3_lock.007s]
  R1 = Resistor [tolerance=±5% resistance=220 package="0402 [SMD]"]

nets:
  N1: Componente1.D6, Componente4.LV4, R1.Pin_1
  N2: Componente1.D7, R1.Pin_0
  GND: Componente1.GND, Componente4.GND, JP1.1
  N3: Componente1.5V, Componente4.LV
  N4: Componente4.HV, JP1.3
  N5: Componente4.HV4, JP1.2
